// Logisim project AssemblyMidtermBernhardt.circ as structural Verilog: 1 circuit, main circuit main
// A+CD'
module main (
);

  wire A_C_out, A_CD_prime_out, A_out, A_prime_B_out, A_prime_B_prime_out, A_prime_D_out, AB_prime_out,
       b_2_out, B_out, B_prime_C_BC_prime_out, B_prime_C_out, B_prime_D_prime_out, BC_prime_out, BD_out,
       c_2_out, C_out, C_prime_CD_out, C_prime_D_out, C_prime_D_prime_out, CD_out, CD_prime_out, d_2_out,
       D_out, D_prime_C_prime_D_out, e_out, f_out, g_out, not_2_out, not_3_out, not_5_out, not_7_out,
       or_1_out, or_2_out, or_3_out, or_4_out, or_5_out, plus_B_prime_D_prime_out, put_d_out, put_f_out,
       put_g_out;

  // NOT_Gate not_1 is placed but not wired
  Button A (.out(A_out));
  Button B (.out(B_out));
  not not_2 (not_2_out, A_out);
  and AB_prime (AB_prime_out, not_3_out, A_out);
  and A_prime_B_prime (A_prime_B_prime_out, not_2_out, not_3_out);
  and A_prime_B (A_prime_B_out, not_2_out, B_out);
  and A_prime_D (A_prime_D_out, not_2_out, D_out);
  Button C (.out(C_out));
  not not_3 (not_3_out, B_out);
  or or_1 (or_1_out, AB_prime_out, A_prime_B_prime_out);
  Button D (.out(D_out));
  // NOT_Gate not_4 is placed but not wired
  not not_5 (not_5_out, C_out);
  and BC_prime (BC_prime_out, B_out, not_5_out);
  and B_prime_C (B_prime_C_out, C_out, not_3_out);
  // NOT_Gate not_6 is placed but not wired
  not not_7 (not_7_out, D_out);
  and CD (CD_out, D_out, C_out);
  and CD_prime (CD_prime_out, C_out, not_7_out);
  and C_prime_D_prime (C_prime_D_prime_out, not_7_out, not_5_out);
  and C_prime_D (C_prime_D_out, D_out, not_5_out);
  or B_prime_C_BC_prime (B_prime_C_BC_prime_out, BC_prime_out, B_prime_C_out);
  or or_2 (or_2_out, CD_out, C_prime_D_prime_out);
  or D_prime_C_prime_D (D_prime_C_prime_D_out, not_7_out, C_prime_D_out);
  and put_d (put_d_out, A_prime_D_out, B_prime_C_BC_prime_out);
  and put_g (put_g_out, B_prime_C_BC_prime_out, not_2_out);
  and put_f (put_f_out, A_prime_B_out, D_prime_C_prime_D_out);
  and BD (BD_out, B_out, D_out);
  and B_prime_D_prime (B_prime_D_prime_out, not_7_out, not_3_out);
  or A_C (A_C_out, C_out, A_out);
  or C_prime_CD (C_prime_CD_out, CD_out, not_5_out);
  or or_3 (or_3_out, A_out, C_prime_D_prime_out);
  or f (f_out, or_3_out, put_f_out);
  or plus_B_prime_D_prime (plus_B_prime_D_prime_out, B_prime_D_prime_out, CD_prime_out);
  or A_CD_prime (A_CD_prime_out, CD_prime_out, A_out);
  or or_4 (or_4_out, BD_out, B_prime_D_prime_out);
  or b_2 (b_2_out, or_1_out, or_2_out);
  or c_2 (c_2_out, A_prime_B_out, C_prime_CD_out);
  or d_2 (d_2_out, put_d_out, plus_B_prime_D_prime_out);
  or g (g_out, put_g_out, A_CD_prime_out);
  or or_5 (or_5_out, or_4_out, A_C_out);
  or e (e_out, B_prime_D_prime_out, CD_prime_out);
  _7_Segment_Display u_7_segment_display_1 (
    .g(g_out), .f(f_out), .a(or_5_out), .b(b_2_out), .e(e_out), .d(d_2_out), .c(c_2_out));  // open: dp
endmodule
