// Logisim project Part2ButDoneIncorrectly.circ as structural Verilog: 1 circuit, main circuit main
module main (
);

  wire and_1_out, and_2_out, and_3_out, and_4_out, clock_1_out, j_k_ff_1_q, j_k_ff_1_qn, j_k_ff_2_q,
       j_k_ff_2_qn, j_k_ff_3_q, j_k_ff_3_qn, not_1_out, not_2_out, or_1_out, or_2_out, or_3_out;

  Clock clock_1 (.out(clock_1_out));
  and and_1 (and_1_out, j_k_ff_2_q, j_k_ff_3_q);
  or or_1 (or_1_out, j_k_ff_2_q, j_k_ff_3_q);
  J_K_Flip_Flop j_k_ff_1 (
    .J(and_1_out), .clk(clock_1_out), .K(or_1_out), .Q(j_k_ff_1_q), .Qn(j_k_ff_1_qn));  // open: preset, en, reset
  and and_2 (and_2_out, j_k_ff_1_qn, j_k_ff_3_q);
  or or_2 (or_2_out, j_k_ff_1_q, j_k_ff_3_q);
  J_K_Flip_Flop j_k_ff_2 (
    .J(and_2_out), .clk(clock_1_out), .K(or_2_out), .Q(j_k_ff_2_q), .Qn(j_k_ff_2_qn));  // open: preset, en, reset
  or or_3 (or_3_out, j_k_ff_2_qn, j_k_ff_1_qn);
  J_K_Flip_Flop j_k_ff_3 (
    .J(or_3_out), .clk(clock_1_out), .K(1'b1), .Q(j_k_ff_3_q), .Qn(j_k_ff_3_qn));  // open: preset, en, reset
  and and_3 (and_3_out, j_k_ff_1_q, j_k_ff_2_qn, j_k_ff_3_qn);
  and and_4 (and_4_out, j_k_ff_1_qn, j_k_ff_2_qn, j_k_ff_3_q);
  not not_1 (not_1_out, and_4_out);
  LED led_1 (.in(not_2_out));
  not not_2 (not_2_out, and_3_out);
  LED led_2 (.in(and_3_out));
  LED led_3 (.in(and_4_out));
  LED led_4 (.in(not_1_out));
endmodule
